# Fritzing sketch FAB_PIC v2.1 (saved by Fritzing 0.9.9b)
circuit board: 10cm x 10cm

parts:
  Componente1 = Arduino Uno (Rev3)
  1 = female alternating pin header, 1 pin [form="♀ (female)"]
  2 = female alternating pin header, 1 pin [form="♀ (female)"]
  3 = female alternating pin header, 1 pin [form="♀ (female)"]
  4 = female alternating pin header, 1 pin [form="♀ (female)"]

nets:
  N1: Componente1.D0/RX, 2.pin1
  N2: Componente1.D1/TX, 1.pin1
  N3: Componente1.5V, 3.pin1
  N4: Componente1.GND, 4.pin1

notes:
  GND
  5V
  TX
  RX
